# Fritzing sketch Wiring Schematic (saved by Fritzing 0.9.3b)
breadboards: 1

parts:
  Part1 = Arduino Uno (Rev3)
  J1 = Basic Servo
  U1 = POT_SWITCH [package=pot_pth]

nets:
  N1: Part1.A0, U1.G$2_1
  GND: Part1.GND, J1.gnd
  N2: Part1.AREF, U1.G$1_E
  N3: Part1.3V3, U1.G$1_A
  5V: Part1.5V, J1.vcc
  N4: U1.G$2_2, U1.G$1_S
